# Fritzing sketch Arduino-Fencing-Scoring-detection-wiring (saved by Fritzing 0.9.3b)

parts:
  Součástka1 = Arduino Uno (Rev3)
  Fencer_1 = Pushbutton [package="[THT]"]
  Fencer_2 = Pushbutton [package="[THT]"]
  R1 = Resistor [tolerance=±5% resistance=100k package="0805 [SMD]"]
  2x = Resistor [tolerance=±5% resistance=100k package="0805 [SMD]"]
  J1 = Piezo Speaker

nets:
  N1: Součástka1.D8, J1.pin2
  N2: Součástka1.D2, Fencer_1.Pin_1, Fencer_1.Pin_2, 2x.Pin_0
  N3: Součástka1.D3_PWM, Fencer_2.Pin_1, Fencer_2.Pin_2, R1.Pin_0
  N4: Součástka1.5V, Fencer_1.Pin_4, Fencer_2.Pin_4
  N5: Součástka1.GND, R1.Pin_1, 2x.Pin_1, J1.pin1
